# Fritzing sketch circuit (saved by Fritzing 0.8.0b)
breadboards: 1

parts:
  LED1 = RGB LED (com. cathode, rbg) [package="5 mm [THT]"]
  Dot_Matrix3 = LED Dot Matrix 18mm (0.7 INCH)
  Raspberry_Pi1 = Raspberry Pi
  Q1 = NPN-Transistor [package="TO92 [THT]"]
  R1 = Resistor [tolerance=±5% resistance=1k package=THT]
  R2 = Resistor [tolerance=±5% resistance=220 package=THT]
  R3 = Resistor [tolerance=±5% resistance=220 package=THT]
  Q2 = NPN-Transistor [package="TO92 [THT]"]
  Q3 = NPN-Transistor [package="TO92 [THT]"]
  R4 = Resistor [tolerance=±5% resistance=220 package=THT]
  R5 = Resistor [tolerance=±5% resistance=220 package=THT]

nets:
  N1: LED1.red_anode, Q3.E
  N2: LED1.common_cathode, R3.Pin_0
  N3: LED1.blue_anode, Q2.E
  N4: Dot_Matrix3.Column_1, Dot_Matrix3.Column_2, Dot_Matrix3.Column_4, Dot_Matrix3.Column_5, Dot_Matrix3.Column_3, Q1.E
  N5: Dot_Matrix3.Row_3, Dot_Matrix3.Row_5, Dot_Matrix3.Row_6, Dot_Matrix3.Row_7, Dot_Matrix3.Row_4, Dot_Matrix3.Row_2, Dot_Matrix3.Row_1, R2.Pin_0
  N6: Raspberry_Pi1.5V, Q1.C, Q2.C, Q3.C
  N7: Raspberry_Pi1.GND, R2.Pin_1, R3.Pin_1
  N8: Raspberry_Pi1.GPIO0, R4.Pin_1
  N9: Raspberry_Pi1.GPIO1, R5.Pin_1
  N10: Raspberry_Pi1.GPIO2, R1.Pin_1
  N11: Q1.B, R1.Pin_0
  N12: Q2.B, R4.Pin_0
  N13: Q3.B, R5.Pin_0
