# Fritzing sketch led (saved by Fritzing 0.8.0b)
breadboards: 1
perfboards: 1

parts:
  Q1 = NPN-Transistor [package="TO92 [THT]"]
  LED1 = LED - 3mm [color="Red (633nm)" package="3 mm [THT]"]
  LED2 = LED - 3mm [color="Red (633nm)" package="3 mm [THT]"]
  LED3 = LED - 3mm [color="Red (633nm)" package="3 mm [THT]"]
  LED4 = LED - 3mm [color="Red (633nm)" package="3 mm [THT]"]
  R1 = Resistor [tolerance=±5% resistance=220 package=THT]
  R2 = Resistor [tolerance=±5% resistance=220 package=THT]
  R3 = Resistor [tolerance=±5% resistance=220 package=THT]
  R4 = Resistor [tolerance=±5% resistance=68 package=THT]
  R5 = Resistor [tolerance=±5% resistance=220 package=THT]

nets:
  N1: Q1.E, LED1.anode, LED2.anode, LED3.anode, LED4.anode
  N2: Q1.B, R5.Pin_1
  5V: Q1.C
  N3: LED1.cathode, R2.Pin_1
  N4: LED2.cathode, R3.Pin_1
  N5: LED3.cathode, R4.Pin_0
  N6: LED4.cathode, R1.Pin_0
  GND: R1.Pin_1, R2.Pin_0, R3.Pin_0, R4.Pin_1
